// Logisim project ProcessadorDedicado.circ as structural Verilog: 12 circuits, main circuit main
module main (
  output [11:0] out_1,
  output [11:0] out_2,
  output [2:0] estadoAtual
);

  wire b1_out, b2_out, blocooperacional_1_c1, blocooperacional_1_c2, blocooperacional_1_regleg_0,
       blocooperacional_1_tc, CK_50KHz_out, divisordefrequencia_1_clock1khz,
       divisordefrequencia_1_clock5omhz, reset_out, unidadedecontrole_1_clearcont,
       unidadedecontrole_1_clearreglg, unidadedecontrole_1_clearreglim, unidadedecontrole_1_clearregtemp,
       unidadedecontrole_1_cleartp, unidadedecontrole_1_clock1khz, unidadedecontrole_1_clock50mhz,
       unidadedecontrole_1_crtlmuxreglim, unidadedecontrole_1_led_0, unidadedecontrole_1_led_1,
       unidadedecontrole_1_loadcont, unidadedecontrole_1_loadreglg, unidadedecontrole_1_loadreglim,
       unidadedecontrole_1_loadregtemp, unidadedecontrole_1_loadtp;
  wire [3:0] blocooperacional_1_d7centena, blocooperacional_1_d7dezena, blocooperacional_1_d7milhar,
       blocooperacional_1_d7unidade;
  wire [4:0] blocooperacional_1_regleds;

  Clock CK_50KHz (.out(CK_50KHz_out));
  DivisorDeFrequencia divisordefrequencia_1 (
    .Clock50Mhz(CK_50KHz_out), .Divisor(12'h1), .clock1KHz(divisordefrequencia_1_clock1khz),
    .clock5OMHz(divisordefrequencia_1_clock5omhz));
  Button b1 (.out(b1_out));
  Button b2 (.out(b2_out));
  Button reset (.out(reset_out));
  LED ledRed_0 (.in(unidadedecontrole_1_led_0));
  UnidadeDeControle unidadedecontrole_1 (
    .b1(b1_out), .b2(b2_out), .reset(reset_out), .tc(blocooperacional_1_tc), .c1(blocooperacional_1_c1),
    .c2(blocooperacional_1_c2), .regLG_0(blocooperacional_1_regleg_0),
    .clk1KHz(divisordefrequencia_1_clock1khz), .clk50MHz(divisordefrequencia_1_clock5omhz),
    .led_0(unidadedecontrole_1_led_0), .led_1(unidadedecontrole_1_led_1),
    .loadCont(unidadedecontrole_1_loadcont), .clearCont(unidadedecontrole_1_clearcont),
    .loadRegLim(unidadedecontrole_1_loadreglim), .clearRegLim(unidadedecontrole_1_clearreglim),
    .crtlMuxRegLim(unidadedecontrole_1_crtlmuxreglim), .LoadRegLG(unidadedecontrole_1_loadreglg),
    .clearRegLG(unidadedecontrole_1_clearreglg), .loadTp(unidadedecontrole_1_loadtp),
    .clearTp(unidadedecontrole_1_cleartp), .loadRegTemp(unidadedecontrole_1_loadregtemp),
    .clearRegTemp(unidadedecontrole_1_clearregtemp), .displayEstadoAtual(estadoAtual),
    .clock1KHz(unidadedecontrole_1_clock1khz), .clock50MHz(unidadedecontrole_1_clock50mhz));
  LED ledRed_1 (.in(unidadedecontrole_1_led_1));
  BlocoOperacional blocooperacional_1 (
    .loadCont(unidadedecontrole_1_loadcont), .clearCont(unidadedecontrole_1_clearcont),
    .loadRegTemp(unidadedecontrole_1_loadregtemp), .clearRegTemp(unidadedecontrole_1_clearregtemp),
    .loadRegLim(unidadedecontrole_1_loadreglim), .clearRegLim(unidadedecontrole_1_clearreglim),
    .crtlMuxRegLim(unidadedecontrole_1_crtlmuxreglim), .loadRegLG(unidadedecontrole_1_loadreglg),
    .clearRegLG(unidadedecontrole_1_clearreglg), .loadTp(unidadedecontrole_1_loadtp),
    .clearTp(unidadedecontrole_1_cleartp), .clock1KHz(unidadedecontrole_1_clock1khz),
    .clock50MHz(unidadedecontrole_1_clock50mhz), .contagem(out_1), .d7Milhar(blocooperacional_1_d7milhar),
    .d7Centena(blocooperacional_1_d7centena), .d7Dezena(blocooperacional_1_d7dezena),
    .d7Unidade(blocooperacional_1_d7unidade), .c1(blocooperacional_1_c1), .Constante(out_2),
    .c2(blocooperacional_1_c2), .RegLeds(blocooperacional_1_regleds), .RegLeg_0(blocooperacional_1_regleg_0),
    .tc(blocooperacional_1_tc));
  Hex_Digit_Display hex_digit_display_1 (.value(blocooperacional_1_d7milhar));  // open: dp
  Hex_Digit_Display hex_digit_display_2 (.value(blocooperacional_1_d7centena));  // open: dp
  LED Led_1 (.in(blocooperacional_1_regleds[3]));
  LED Led_0 (.in(blocooperacional_1_regleds[4]));
  Hex_Digit_Display hex_digit_display_3 (.value(blocooperacional_1_d7dezena));  // open: dp
  Hex_Digit_Display hex_digit_display_4 (.value(blocooperacional_1_d7unidade));  // open: dp
  LED Led_2 (.in(blocooperacional_1_regleds[2]));
  LED Led_4 (.in(blocooperacional_1_regleds[0]));
  LED Led_3 (.in(blocooperacional_1_regleds[1]));

  // Notes on the sheet:
  //   DIsplays de 7 segmentos
endmodule

module Cont (
  input  load,
  input  clk,
  input  clear,
  output [11:0] cont
);

  wire [11:0] adder_1_out;

  Register #(.width(12)) register_1 (.D(adder_1_out), .en(load), .clk(clk), .Q(cont), .clr(clear));
  Adder #(.width(12)) adder_1 (.a(cont), .b(12'h1), .out(adder_1_out));  // open: cin, cout
endmodule

module RegLim (
  input  muxControl,
  input  load,
  input  clk,
  input  clear,
  output [11:0] RegLim
);

  wire [11:0] multiplexer_1_out, shifter_1_out;

  Multiplexer #(.width(12), .enable("false")) multiplexer_1 (
    .in0(shifter_1_out), .in1(12'hfa0), .out(multiplexer_1_out), .sel(muxControl));
  Shifter #(.width(12), .shift("lr")) shifter_1 (.in(RegLim), .\dist (4'b0001), .out(shifter_1_out));
  Register #(.width(12)) register_1 (.D(multiplexer_1_out), .en(load), .clk(clk), .Q(RegLim), .clr(clear));
endmodule

module RegLG (
  input  load,
  input  clk,
  input  clr,
  output [4:0] RegLG
);

  wire [4:0] not_1_out, not_2_out, shifter_1_out;

  Shifter #(.width(5), .shift("lr")) shifter_1 (.in(not_2_out), .\dist (3'b001), .out(shifter_1_out));
  Register #(.width(5)) register_1 (.D(not_1_out), .en(load), .clk(clk), .Q(RegLG), .clr(clr));
  assign not_1_out = ~shifter_1_out;  // NOT_Gate not_1, 5 bits wide
  assign not_2_out = ~RegLG;  // NOT_Gate not_2, 5 bits wide
endmodule

module Tp (
  input  load,
  input  clk,
  input  clear,
  output out_4
);

  wire [9:0] adder_1_out, register_1_q;

  Register #(.width(10)) register_1 (.D(adder_1_out), .en(load), .clk(clk), .Q(register_1_q), .clr(clear));
  Adder #(.width(10)) adder_1 (.a(register_1_q), .b(10'h1), .out(adder_1_out));  // open: cin, cout
  Comparator #(.width(10), .mode("unsigned")) comparator_1 (.a(register_1_q), .b(10'h3e7), .eq(out_4));  // open: gt, lt
endmodule

module RegTemp (
  input  clk,
  input  [11:0] Cont,
  input  load,
  input  clr,
  output [3:0] out_5,
  output [3:0] out_6,
  output [3:0] out_7,
  output [3:0] out_8
);

  wire and_1_out, and_2_out, and_3_out, comparator_1_eq, comparator_1_gt, comparator_1_lt, comparator_2_eq,
       comparator_2_gt, comparator_2_lt, comparator_3_eq, comparator_3_gt, comparator_3_lt, comparator_4_eq,
       comparator_4_gt, comparator_4_lt, d_ff_1_q, d_ff_2_q, d_ff_3_q, d_ff_4_q, d_ff_5_q, d_ff_6_q,
       d_ff_7_q, d_ff_8_q, d_ff_9_q, d_ff_10_q, or_1_out, or_2_out, or_3_out, or_4_out, or_5_out, or_6_out,
       or_7_out, or_8_out;
  wire [3:0] adder_1_out, adder_2_out, adder_3_out, adder_4_out, register_6_q, register_7_q, register_8_q,
       register_9_q, register_12_q;
  wire [11:0] multiplexer_1_out, multiplexer_2_out, multiplexer_3_out, multiplexer_4_out, register_1_q,
       register_2_q, register_3_q, register_4_q, register_5_q, subtractor_1_out, subtractor_2_out,
       subtractor_3_out, subtractor_4_out;

  Register #(.width(12)) register_1 (.D(Cont), .en(load), .clk(clk), .Q(register_1_q), .clr(clr));
  D_Flip_Flop d_ff_1 (.D(comparator_1_lt), .clk(clk), .Q(d_ff_1_q), .preset(clr));  // open: Qn, reset
  D_Flip_Flop d_ff_2 (.D(comparator_2_lt), .clk(clk), .Q(d_ff_2_q), .preset(clr));  // open: Qn, reset
  D_Flip_Flop d_ff_3 (.D(comparator_3_lt), .clk(clk), .Q(d_ff_3_q));  // open: Qn, preset, reset
  D_Flip_Flop d_ff_4 (.D(load), .clk(clk), .Q(d_ff_4_q), .reset(clr));  // open: Qn, preset
  D_Flip_Flop d_ff_5 (.D(d_ff_1_q), .clk(clk), .Q(d_ff_5_q), .preset(clr));  // open: Qn, reset
  D_Flip_Flop d_ff_6 (.D(and_1_out), .clk(clk), .Q(d_ff_6_q), .reset(clr));  // open: Qn, preset
  and and_1 (and_1_out, ~d_ff_5_q, d_ff_1_q);  // AND_Gate
  D_Flip_Flop d_ff_7 (.D(d_ff_2_q), .clk(clk), .Q(d_ff_7_q), .preset(clr));  // open: Qn, reset
  D_Flip_Flop d_ff_8 (.D(and_2_out), .clk(clk), .Q(d_ff_8_q), .reset(clr));  // open: Qn, preset
  and and_2 (and_2_out, ~d_ff_7_q, d_ff_2_q);  // AND_Gate
  D_Flip_Flop d_ff_9 (.D(d_ff_3_q), .clk(clk), .Q(d_ff_9_q));  // open: Qn, preset, reset
  D_Flip_Flop d_ff_10 (.D(and_3_out), .clk(clk), .Q(d_ff_10_q), .reset(clr));  // open: Qn, preset
  and and_3 (and_3_out, ~d_ff_9_q, d_ff_3_q);  // AND_Gate
  or or_1 (or_1_out, d_ff_4_q, or_5_out);
  or or_2 (or_2_out, d_ff_6_q, or_6_out);
  or or_3 (or_3_out, d_ff_8_q, or_7_out);
  or or_4 (or_4_out, d_ff_10_q, or_8_out);
  Register #(.width(12)) register_2 (.D(multiplexer_1_out), .en(or_1_out), .clk(clk), .Q(register_2_q), .clr(clr));
  Multiplexer #(.width(12), .enable("false")) multiplexer_1 (
    .in0(subtractor_1_out), .in1(register_1_q), .out(multiplexer_1_out), .sel(d_ff_4_q));
  Register #(.width(12)) register_3 (.D(multiplexer_2_out), .en(or_2_out), .clk(clk), .Q(register_3_q), .clr(clr));
  Multiplexer #(.width(12), .enable("false")) multiplexer_2 (
    .in0(subtractor_2_out), .in1(register_2_q), .out(multiplexer_2_out), .sel(d_ff_6_q));
  Register #(.width(12)) register_4 (.D(multiplexer_3_out), .en(or_3_out), .clk(clk), .Q(register_4_q), .clr(clr));
  Multiplexer #(.width(12), .enable("false")) multiplexer_3 (
    .in0(subtractor_3_out), .in1(register_3_q), .out(multiplexer_3_out), .sel(d_ff_8_q));
  Register #(.width(12)) register_5 (.D(multiplexer_4_out), .en(or_4_out), .clk(clk), .Q(register_5_q), .clr(clr));
  Multiplexer #(.width(12), .enable("false")) multiplexer_4 (
    .in0(subtractor_4_out), .in1(register_4_q), .out(multiplexer_4_out), .sel(d_ff_10_q));
  Subtractor #(.width(12)) subtractor_1 (.a(register_2_q), .b(12'h3e8), .out(subtractor_1_out));  // open: bin, bout
  Subtractor #(.width(12)) subtractor_2 (.a(register_3_q), .b(12'h64), .out(subtractor_2_out));  // open: bin, bout
  Subtractor #(.width(12)) subtractor_3 (.a(register_4_q), .b(12'ha), .out(subtractor_3_out));  // open: bin, bout
  Subtractor #(.width(12)) subtractor_4 (.a(register_5_q), .b(12'h1), .out(subtractor_4_out));  // open: bin, bout
  Comparator #(.width(12), .mode("unsigned")) comparator_1 (
    .a(register_2_q), .b(12'h3e8), .gt(comparator_1_gt), .eq(comparator_1_eq), .lt(comparator_1_lt));
  Comparator #(.width(12), .mode("unsigned")) comparator_2 (
    .a(register_3_q), .b(12'h64), .gt(comparator_2_gt), .eq(comparator_2_eq), .lt(comparator_2_lt));
  Comparator #(.width(12), .mode("unsigned")) comparator_3 (
    .a(register_4_q), .b(12'ha), .gt(comparator_3_gt), .eq(comparator_3_eq), .lt(comparator_3_lt));
  Comparator #(.width(12), .mode("unsigned")) comparator_4 (
    .a(register_5_q), .b(12'h1), .gt(comparator_4_gt), .eq(comparator_4_eq), .lt(comparator_4_lt));
  or or_5 (or_5_out, comparator_1_gt, comparator_1_eq);
  or or_6 (or_6_out, comparator_2_gt, comparator_2_eq);
  or or_7 (or_7_out, comparator_3_gt, comparator_3_eq);
  or or_8 (or_8_out, comparator_4_gt, comparator_4_eq);
  Register #(.width(4)) register_6 (.D(adder_1_out), .en(or_5_out), .clk(clk), .Q(register_6_q), .clr(clr));
  Adder #(.width(4)) adder_1 (.a(register_6_q), .b(4'b0001), .out(adder_1_out));  // open: cin, cout
  Register #(.width(4)) register_7 (.D(adder_2_out), .en(or_6_out), .clk(clk), .Q(register_7_q), .clr(clr));
  Adder #(.width(4)) adder_2 (.a(register_7_q), .b(4'b0001), .out(adder_2_out));  // open: cin, cout
  Register #(.width(4)) register_8 (.D(adder_3_out), .en(or_7_out), .clk(clk), .Q(register_8_q), .clr(clr));
  Adder #(.width(4)) adder_3 (.a(register_8_q), .b(4'b0001), .out(adder_3_out));  // open: cin, cout
  Register #(.width(4)) register_9 (.D(adder_4_out), .en(or_8_out), .clk(clk), .Q(register_9_q), .clr(clr));
  Adder #(.width(4)) adder_4 (.a(register_9_q), .b(4'b0001), .out(adder_4_out));  // open: cin, cout
  Register #(.width(4)) register_10 (.D(register_6_q), .en(comparator_1_lt), .clk(clk), .clr(clr));  // open: Q
  Register #(.width(4)) register_11 (.D(register_7_q), .en(comparator_2_lt), .clk(clk), .clr(clr));  // open: Q
  Register #(.width(4)) register_12 (.D(register_8_q), .en(comparator_3_lt), .clk(clk), .Q(register_12_q), .clr(clr));
  Register #(.width(4)) register_13 (.D(register_9_q), .en(comparator_4_lt), .clk(clk), .clr(clr));  // open: Q
  Hex_Digit_Display hex_digit_display_1 (.value(out_5));  // open: dp
  // Binairy_to_BCD_converter #(.binvalue(12)) binairy_to_bcd_converter_1: pin names not known; wires that end beside it: register_12_q, register_1_q, out_5, out_6, out_7, out_8
  Hex_Digit_Display hex_digit_display_2 (.value(out_6));  // open: dp
  Hex_Digit_Display hex_digit_display_3 (.value(out_7));  // open: dp
  Hex_Digit_Display hex_digit_display_4 (.value(out_8));  // open: dp
endmodule

module dispDriver (
  input  [3:0] in_1,
  output a,
  output b,
  output c,
  output d,
  output e,
  output f,
  output g
);

  wire and_1_out, and_2_out, and_3_out, and_4_out, and_5_out, and_6_out, and_7_out, and_8_out, and_9_out;

  and and_1 (and_1_out, in_1[2], in_1[0]);
  and and_2 (and_2_out, ~in_1[2], ~in_1[0]);  // AND_Gate
  and and_3 (and_3_out, ~in_1[1], ~in_1[0]);  // AND_Gate
  and and_4 (and_4_out, in_1[1], in_1[0]);
  and and_5 (and_5_out, in_1[1], ~in_1[0]);  // AND_Gate
  and and_6 (and_6_out, in_1[2], ~in_1[1], in_1[0]);  // AND_Gate
  and and_7 (and_7_out, ~in_1[2], in_1[1]);  // AND_Gate
  and and_8 (and_8_out, in_1[2], ~in_1[0]);  // AND_Gate
  and and_9 (and_9_out, in_1[2], ~in_1[1]);  // AND_Gate
  or or_1 (a, and_1_out, in_1[3], in_1[1], and_2_out);
  or or_2 (b, and_3_out, ~in_1[2], and_4_out);  // OR_Gate
  or or_3 (c, in_1[2], ~in_1[1], in_1[0]);  // OR_Gate
  or or_4 (d, and_2_out, and_5_out, and_6_out, and_7_out, in_1[3]);
  or or_5 (e, and_2_out, and_5_out);
  or or_6 (f, in_1[3], and_3_out, and_9_out, and_8_out);
  or or_7 (g, in_1[3], and_9_out, and_7_out, and_5_out);
  _7_Segment_Display u_7_segment_display_1 (.g(g), .f(f), .a(a), .b(b), .e(e), .d(d), .c(c));  // open: dp
endmodule

module DivisorDeFrequencia (
  input  Clock50Mhz,
  input  [11:0] Divisor,
  output clock1KHz,
  output clock5OMHz
);

  wire comparator_1_gt, comparator_1_lt;
  wire [11:0] Contador_q;

  Counter #(.width(12), .max('hfff)) Contador (
    .clr(comparator_1_gt), .up(1'b1), .clk(Clock50Mhz), .Q(Contador_q));  // open: load, count, D, carry
  Comparator #(.width(12), .mode("unsigned")) comparator_1 (
    .a(Contador_q), .b(Divisor), .gt(comparator_1_gt), .lt(comparator_1_lt));  // open: eq
  or or_1 (clock1KHz, comparator_1_gt, comparator_1_lt);

  assign clock5OMHz = Clock50Mhz;
endmodule

module RegistradoresDeEstados (
  input  [2:0] ProximoEstado,
  input  clk,
  output [2:0] estadoAtual,
  output clock
);

  Register #(.width(3)) register_1 (.D(ProximoEstado), .en(1'b1), .clk(clk), .Q(estadoAtual));  // open: clr

  assign clock = clk;
endmodule

module UnidadeDeControle (
  input  b1,
  input  b2,
  input  reset,
  input  tc,
  input  c1,
  input  c2,
  input  regLG_0,
  input  clk1KHz,
  input  clk50MHz,
  output led_0,
  output led_1,
  output loadCont,
  output clearCont,
  output loadRegLim,
  output clearRegLim,
  output crtlMuxRegLim,
  output LoadRegLG,
  output clearRegLG,
  output loadTp,
  output clearTp,
  output loadRegTemp,
  output clearRegTemp,
  output [2:0] displayEstadoAtual,
  output clock1KHz,
  output clock50MHz
);

  wire [2:0] logicacombinacional_1_proximoestado, registradoresdeestados_1_estadoatual;

  LogicaCombinacional logicacombinacional_1 (
    .b1(b1), .b2(b2), .reset(reset), .tc(tc), .c1(c1), .c2(c2), .regLG_0(regLG_0),
    .estadoAtual(registradoresdeestados_1_estadoatual), .led_0(led_0), .led_1(led_1), .loadCont(loadCont),
    .clearCont(clearCont), .loadRegLim(loadRegLim), .clearRegLim(clearRegLim), .crtlMuxRegLim(crtlMuxRegLim),
    .loadRegLG(LoadRegLG), .clearRegLG(clearRegLG), .loadTp(loadTp), .clearTp(clearTp),
    .loadRegTemp(loadRegTemp), .clearRegTemp(clearRegTemp), .displayEstadoAtual(displayEstadoAtual),
    .proximoEstado(logicacombinacional_1_proximoestado));
  RegistradoresDeEstados registradoresdeestados_1 (
    .ProximoEstado(logicacombinacional_1_proximoestado), .clk(clk1KHz),
    .estadoAtual(registradoresdeestados_1_estadoatual), .clock(clock1KHz));

  assign clock50MHz = clk50MHz;
endmodule

module LogicaCombinacional (
  input  b1,
  input  b2,
  input  reset,
  input  tc,
  input  c1,
  input  c2,
  input  regLG_0,
  input  [2:0] estadoAtual,
  output led_0,
  output led_1,
  output loadCont,
  output clearCont,
  output loadRegLim,
  output clearRegLim,
  output crtlMuxRegLim,
  output loadRegLG,
  output clearRegLG,
  output loadTp,
  output clearTp,
  output loadRegTemp,
  output clearRegTemp,
  output [2:0] displayEstadoAtual,
  output [2:0] proximoEstado
);

  wire and_1_out, and_2_out, and_3_out, and_4_out, and_5_out, and_6_out, and_7_out, and_8_out, and_9_out,
       and_10_out, and_11_out, and_12_out, and_13_out, and_14_out, and_15_out, and_16_out, and_17_out,
       and_18_out, and_19_out, and_20_out, and_24_out, and_31_out, and_33_out, and_34_out;

  and and_1 (and_1_out, ~estadoAtual[0], ~estadoAtual[1], ~estadoAtual[2]);  // AND_Gate
  and and_2 (and_2_out, estadoAtual[0], ~estadoAtual[1], ~estadoAtual[2]);  // AND_Gate
  and and_3 (and_3_out, ~estadoAtual[0], estadoAtual[1], ~estadoAtual[2]);  // AND_Gate
  and and_4 (and_4_out, estadoAtual[0], estadoAtual[1], ~estadoAtual[2]);  // AND_Gate
  and and_5 (and_5_out, ~estadoAtual[0], ~estadoAtual[1], estadoAtual[2]);  // AND_Gate
  and and_6 (and_6_out, estadoAtual[0], ~estadoAtual[1], estadoAtual[2]);  // AND_Gate
  and and_7 (and_7_out, ~estadoAtual[0], estadoAtual[1], estadoAtual[2]);  // AND_Gate
  and and_8 (and_8_out, ~reset, and_6_out);  // AND_Gate
  and and_9 (and_9_out, ~tc, and_7_out);  // AND_Gate
  and and_10 (and_10_out, c2, and_4_out);
  and and_11 (and_11_out, b2, ~c2, and_4_out);  // AND_Gate
  or or_1 (proximoEstado[2], and_9_out, and_8_out, and_5_out, and_10_out, and_11_out);
  and and_12 (and_12_out, ~tc, and_7_out);  // AND_Gate
  and and_13 (and_13_out, ~b2, ~c2, and_4_out);  // AND_Gate
  or or_2 (proximoEstado[1], and_12_out, and_5_out, and_13_out, and_3_out, and_14_out);
  and and_14 (and_14_out, c1, and_2_out);
  and and_15 (and_15_out, ~regLG_0, tc, and_7_out);  // AND_Gate
  or or_3 (proximoEstado[0], and_15_out, and_16_out, and_17_out, and_18_out, and_3_out, and_19_out, and_20_out);
  and and_16 (and_16_out, ~reset, and_6_out);  // AND_Gate
  and and_17 (and_17_out, c2, and_4_out);
  and and_18 (and_18_out, ~b2, ~c2, and_4_out);  // AND_Gate
  and and_19 (and_19_out, ~c1, and_2_out);  // AND_Gate
  and and_20 (and_20_out, b1, and_1_out);
  and and_21 (led_0, ~estadoAtual[2], estadoAtual[1]);  // AND_Gate
  and and_22 (led_1, estadoAtual[2], estadoAtual[0]);
  and and_23 (loadCont, ~estadoAtual[2], estadoAtual[0]);  // AND_Gate
  and and_24 (and_24_out, ~estadoAtual[2], ~estadoAtual[0]);  // AND_Gate
  and and_25 (loadRegLim, ~estadoAtual[1], ~estadoAtual[0]);  // AND_Gate
  and and_26 (crtlMuxRegLim, ~estadoAtual[2], ~estadoAtual[1], ~estadoAtual[0]);  // AND_Gate
  and and_27 (loadRegLG, estadoAtual[2], ~estadoAtual[1], ~estadoAtual[0]);  // AND_Gate
  and and_28 (clearRegLG, ~estadoAtual[2], ~estadoAtual[1], ~estadoAtual[0]);  // AND_Gate
  and and_29 (loadTp, estadoAtual[2], estadoAtual[1]);
  and and_30 (clearTp, ~estadoAtual[1], ~estadoAtual[0]);  // AND_Gate
  and and_31 (and_31_out, estadoAtual[1], estadoAtual[0]);
  and and_32 (clearRegTemp, ~estadoAtual[2], ~estadoAtual[1]);  // AND_Gate
  and and_33 (and_33_out, ~estadoAtual[2], estadoAtual[1], ~estadoAtual[0]);  // AND_Gate
  and and_34 (and_34_out, estadoAtual[2], ~estadoAtual[1], ~estadoAtual[0]);  // AND_Gate
  or or_4 (clearCont, and_33_out, and_24_out);
  or or_5 (loadRegTemp, and_34_out, and_31_out);

  assign clearRegLim = 1'b0;
  assign displayEstadoAtual = estadoAtual;
endmodule

module BlocoOperacional (
  input  loadCont,
  input  clearCont,
  input  loadRegTemp,
  input  clearRegTemp,
  input  loadRegLim,
  input  clearRegLim,
  input  crtlMuxRegLim,
  input  loadRegLG,
  input  clearRegLG,
  input  loadTp,
  input  clearTp,
  input  clock1KHz,
  input  clock50MHz,
  output [11:0] contagem,
  output [3:0] d7Milhar,
  output [3:0] d7Centena,
  output [3:0] d7Dezena,
  output [3:0] d7Unidade,
  output c1,
  output [11:0] Constante,
  output c2,
  output [4:0] RegLeds,
  output RegLeg_0,
  output tc
);

  wire and_1_out, comparator_2_eq, comparator_2_gt;
  wire [11:0] reglim_1_reglim;

  Cont cont_1 (.load(loadCont), .clk(clock1KHz), .clear(clearCont), .cont(contagem));
  RegLG reglg_1 (.load(loadRegLG), .clk(clock1KHz), .clr(clearRegLG), .RegLG(RegLeds));
  Tp tp_1 (.load(loadTp), .clk(clock1KHz), .clear(clearTp), .out_4(tc));
  RegLim reglim_1 (
    .muxControl(crtlMuxRegLim), .load(loadRegLim), .clk(clock1KHz), .clear(clearRegLim),
    .RegLim(reglim_1_reglim));
  Random #(.width(12)) RegistradorPN (.clk(and_1_out), .out(Constante));  // open: clr, next
  and and_1 (and_1_out, clock1KHz, clock50MHz);
  Comparator #(.width(12), .mode("unsigned")) comparator_1 (.a(contagem), .b(Constante), .eq(c1));  // open: gt, lt
  Comparator #(.width(12), .mode("unsigned")) comparator_2 (
    .a(contagem), .b(reglim_1_reglim), .gt(comparator_2_gt), .eq(comparator_2_eq));  // open: lt
  RegTemp regtemp_1 (
    .clk(clock1KHz), .Cont(contagem), .load(loadRegTemp), .clr(clearRegTemp), .out_5(d7Milhar),
    .out_6(d7Centena), .out_7(d7Dezena), .out_8(d7Unidade));
  or or_1 (c2, comparator_2_gt, comparator_2_eq);

  assign RegLeg_0 = RegLeds[0];
endmodule
